// Logisim project elevator_controller.circ as structural Verilog
module main (
  input  in_1,
  input  in_2,
  input  in_3,
  input  in_4
);

  wire and_1_out, and_2_out, and_3_out, and_4_out, and_5_out, button_1_out, button_2_out, button_3_out,
       button_4_out, button_5_out, button_6_out, button_7_out, button_8_out, button_9_out, button_10_out,
       button_11_out, button_12_out, button_13_out, button_14_out, button_15_out, button_16_out, clock_1_out,
       clock_2_out, ic_7485_1_p1, j_k_ff_1_q, j_k_ff_1_qn, j_k_ff_2_q, j_k_ff_2_qn, n7448_1_p9, n7448_1_p10,
       n7448_1_p11, n7448_1_p12, n7448_1_p13, n7448_1_p14, n7448_1_p15, n7474_1_p5, n7474_1_p13, n7474_2_p7,
       n74138_1_p7, n74138_1_p10, n74138_1_p11, n74138_1_p12, n74138_1_p13, n74138_1_p14, n74138_1_p15,
       n74148_1_p5, n74148_1_p6, n74148_1_p15, nand_1_out, not_1_out, not_4_out, not_5_out, not_6_out,
       not_7_out, not_8_out, not_9_out, not_10_out, not_11_out, not_12_out, not_13_out, not_14_out,
       not_15_out, not_16_out, or_1_out, or_2_out;
  wire [2:0] n7448_1_p2, n7474_1_p6;

  Decoder #(.select(4)) decoder_1 (
    .out0(in_1), .out1(in_1));  // open: out2, out3, out4, out5, out6, out7, out8, out9, out10, out11, out12, out13, out14, out15, sel, en
  Button button_1 (.out(button_1_out));
  Button button_2 (.out(button_2_out));
  Button button_3 (.out(button_3_out));
  Button button_4 (.out(button_4_out));
  Button button_5 (.out(button_5_out));
  Button button_6 (.out(button_6_out));
  Button button_7 (.out(button_7_out));
  Button button_8 (.out(button_8_out));
  // IC_7485 ic_7485_1: pin names not known; wires that end beside it: ic_7485_1_p1
  Button button_9 (.out(button_9_out));
  Button button_10 (.out(button_10_out));
  Button button_11 (.out(button_11_out));
  Button button_12 (.out(button_12_out));
  Button button_13 (.out(button_13_out));
  Button button_14 (.out(button_14_out));
  Button button_15 (.out(button_15_out));
  Button button_16 (.out(button_16_out));
  not not_1 (not_1_out, button_1_out);
  not not_2 (not_1_out, button_2_out);
  not not_3 (not_1_out, button_3_out);
  not not_4 (not_4_out, button_4_out);
  not not_5 (not_5_out, button_5_out);
  not not_6 (not_6_out, button_6_out);
  not not_7 (not_7_out, button_7_out);
  Priority_Encoder priority_encoder_1 (
    .in0(button_9_out), .in1(button_10_out), .in2(button_11_out), .in3(button_12_out), .in4(button_13_out),
    .in5(button_14_out), .in6(button_15_out), .in7(button_16_out), .en_out(ic_7485_1_p1));  // open: out, en_in, gs
  // _7400_lib_74148 74148_1: pin names not known; wires that end beside it: not_4_out, not_1_out, not_1_out, not_1_out, n74148_1_p5, n74148_1_p6, 1'b0, not_1_out, not_7_out, 1'b1, not_5_out, not_6_out, not_7_out, not_7_out, n74148_1_p15
  Multiplexer #(.width(4)) multiplexer_1 ();  // open: in0, in1, out, sel, en
  nand nand_1 (nand_1_out, not_1_out, not_4_out, not_5_out, not_6_out, not_7_out);
  Decoder #(.select(4)) decoder_2 ();  // open: out0, out1, out2, out3, out4, out5, out6, out7, out8, out9, out10, out11, out12, out13, out14, out15, sel, en
  Clock clock_1 (.out(clock_1_out));
  and and_1 (and_1_out, nand_1_out, clock_1_out);
  // _7474 7474_1: pin names not known; wires that end beside it: button_8_out, n74148_1_p6, and_1_out, 1'b0, n7474_1_p5, n7474_1_p6[0], 1'b0, 1'b1, button_8_out, n74148_1_p5, and_1_out, 1'b0, n7474_1_p13, n7474_1_p6[1]
  // _7474 7474_2: pin names not known; wires that end beside it: 1'b0, 1'b1, button_8_out, n74148_1_p15, and_1_out, 1'b0, n7474_2_p7, n7474_1_p6[2]
  LED led_1 (.in(n7474_1_p13));
  LED led_2 (.in(n7474_1_p5));
  LED led_3 (.in(n7474_2_p7));
  Clock #(.highDuration(30), .lowDuration(30)) clock_2 (.out(clock_2_out));
  not not_8 (not_8_out, clock_2_out);
  J_K_Flip_Flop j_k_ff_1 (
    .J(in_4), .clk(not_8_out), .K(in_4), .Q(j_k_ff_1_q), .Qn(j_k_ff_1_qn), .en(in_4));  // open: preset, reset
  not not_9 (not_9_out, in_3);
  and and_2 (and_2_out, in_3, j_k_ff_2_q, j_k_ff_1_q);
  and and_3 (and_3_out, j_k_ff_2_qn, j_k_ff_1_qn, not_9_out);
  J_K_Flip_Flop j_k_ff_2 (
    .J(or_2_out), .clk(not_8_out), .K(or_2_out), .Q(j_k_ff_2_q), .Qn(j_k_ff_2_qn));  // open: preset, en, reset
  or or_1 (or_1_out, and_2_out, and_3_out);
  J_K_Flip_Flop j_k_ff_3 ();  // open: J, clk, K, Q, Qn, preset, en, reset
  J_K_Flip_Flop j_k_ff_4 (.J(or_1_out), .clk(not_8_out), .K(or_1_out), .en(in_4));  // open: Q, Qn, preset, reset
  J_K_Flip_Flop j_k_ff_5 ();  // open: J, clk, K, Q, Qn, preset, en, reset
  // _7448 7448_1: pin names not known; wires that end beside it: 1'b1, n7448_1_p2[0], 1'b1, 1'b1, 1'b0, n7448_1_p2[2], 1'b0, 1'b1, n7448_1_p9, n7448_1_p10, n7448_1_p11, n7448_1_p12, n7448_1_p13, n7448_1_p14, n7448_1_p15
  and and_4 (and_4_out, in_3, j_k_ff_1_q);
  or or_2 (or_2_out, and_4_out, and_5_out);
  and and_5 (and_5_out, j_k_ff_1_qn, not_9_out);
  // _74138 74138_1: pin names not known; wires that end beside it: n7448_1_p2[2], 1'b1, n7448_1_p2[0], 1'b0, 1'b0, 1'b1, n74138_1_p7, 1'b0, 1'b1, n74138_1_p10, n74138_1_p11, n74138_1_p12, n74138_1_p13, n74138_1_p14, n74138_1_p15
  _7_Segment_Display u_7_segment_display_1 (
    .g(n7448_1_p10), .f(n7448_1_p9), .a(n7448_1_p11), .b(n7448_1_p12), .e(n7448_1_p15), .d(n7448_1_p14),
    .c(n7448_1_p13));  // open: dp
  not not_10 (not_10_out, n74138_1_p7);
  not not_11 (not_11_out, n74138_1_p15);
  not not_12 (not_12_out, n74138_1_p14);
  not not_13 (not_13_out, n74138_1_p13);
  not not_14 (not_14_out, n74138_1_p12);
  not not_15 (not_15_out, n74138_1_p11);
  not not_16 (not_16_out, n74138_1_p10);
  LED led_4 (.in(not_10_out));
  LED led_5 (.in(not_11_out));
  LED led_6 (.in(not_12_out));
  LED led_7 (.in(not_13_out));
  LED led_8 (.in(not_14_out));
  LED led_9 (.in(not_15_out));
  LED led_10 (.in(not_16_out));

  assign in_2 = in_1;
  // also tied to VCC on the sheet: not_7_out
endmodule
