// Logisim project first.circ as structural Verilog: 1 circuit, main circuit main
module main (
  input  Floor_1,
  input  Floor_2,
  input  Floor_3,
  input  Floor_4,
  input  Floor_5,
  input  Floor_6,
  input  Floor_7,
  input  Reset
);

  wire d_ff_1_p1, d_ff_2_p1, n555_timer_1_p1, n555_timer_1_p2, n555_timer_1_p3, n555_timer_1_p7,
       n7447_bcd_to_7_segment_decoder_1_p1, n7447_bcd_to_7_segment_decoder_1_p2, n7485_comparator_1_p1,
       n7485_comparator_1_p3, n74148_priority_encoder_1_p9, n74148_priority_encoder_1_p10,
       n74148_priority_encoder_1_p11, n74148_priority_encoder_1_p12, n74148_priority_encoder_1_p13,
       n74148_priority_encoder_1_p14, n74148_priority_encoder_1_p15, n74148_priority_encoder_1_p16,
       n74148_priority_encoder_1_p25, n74193_u_d_counter_1_p1, n74193_u_d_counter_1_p2,
       n74193_u_d_counter_1_p5, n74193_u_d_counter_1_p6, n74193_u_d_counter_1_p7, n74193_u_d_counter_1_p8,
       n74193_u_d_counter_1_p9, n74193_u_d_counter_1_p10;

  // _74148_Priority_Encoder 74148_priority_encoder_1: pin names not known; wires that end beside it: Floor_1, Floor_2, Floor_3, Floor_4, Floor_5, Floor_6, Floor_7, Reset, n74148_priority_encoder_1_p9, n74148_priority_encoder_1_p10, n74148_priority_encoder_1_p11, n74148_priority_encoder_1_p12, n74148_priority_encoder_1_p13, n74148_priority_encoder_1_p14, n74148_priority_encoder_1_p15, n74148_priority_encoder_1_p16, n74148_priority_encoder_1_p9, n74148_priority_encoder_1_p10, n74148_priority_encoder_1_p11, n74148_priority_encoder_1_p12, n74148_priority_encoder_1_p13, n74148_priority_encoder_1_p14, n74148_priority_encoder_1_p15, n74148_priority_encoder_1_p16, n74148_priority_encoder_1_p25
  // D_Flip_Flop d_ff_1: pin names not known; wires that end beside it: d_ff_1_p1, n74148_priority_encoder_1_p25
  // D_Flip_Flop d_ff_2: pin names not known; wires that end beside it: d_ff_2_p1, d_ff_1_p1
  // D_Flip_Flop d_ff_3: pin names not known; wires that end beside it: d_ff_2_p1
  // _555_Timer #(.R1("1k"), .R2("5M"), .C("0.1uF")) 555_timer_1: pin names not known; wires that end beside it: n555_timer_1_p1, n555_timer_1_p2, n555_timer_1_p3, n555_timer_1_p1, n555_timer_1_p2, n555_timer_1_p3, n555_timer_1_p7
  // _7485_Comparator 7485_comparator_1: pin names not known; wires that end beside it: n7485_comparator_1_p1, n555_timer_1_p7, n7485_comparator_1_p3
  // AND_Gate and_1: pin names not known; wires that end beside it: n7485_comparator_1_p1
  // AND_Gate and_2: pin names not known; wires that end beside it: n7485_comparator_1_p3
  // _74193_U_D_Counter 74193_u_d_counter_1: pin names not known; wires that end beside it: n74193_u_d_counter_1_p1, n74193_u_d_counter_1_p2, n74193_u_d_counter_1_p1, n74193_u_d_counter_1_p2, n74193_u_d_counter_1_p5, n74193_u_d_counter_1_p6, n74193_u_d_counter_1_p7, n74193_u_d_counter_1_p8, n74193_u_d_counter_1_p9, n74193_u_d_counter_1_p10
  // _7447_BCD_to_7_Segment_Decoder 7447_bcd_to_7_segment_decoder_1: pin names not known; wires that end beside it: n7447_bcd_to_7_segment_decoder_1_p1, n7447_bcd_to_7_segment_decoder_1_p2
  // _7_Segment_Display 7_segment_display_1: pin names not known; wires that end beside it: n7447_bcd_to_7_segment_decoder_1_p2
  LED led_1 (.in(n74193_u_d_counter_1_p5));
  LED led_2 (.in(n74193_u_d_counter_1_p6));
  LED led_3 (.in(n74193_u_d_counter_1_p7));
  LED led_4 (.in(n7447_bcd_to_7_segment_decoder_1_p1));
  LED led_5 (.in(n74193_u_d_counter_1_p8));
  LED led_6 (.in(n74193_u_d_counter_1_p9));
  LED led_7 (.in(n74193_u_d_counter_1_p10));
endmodule
