// Logisim project mod-8 카운터.circ as structural Verilog: 1 circuit, main circuit main
module main (
  input  en
);

  wire and_1_out, and_2_out, clock_1_out, decoder_1_out0, decoder_1_out1, decoder_1_out2, decoder_1_out3,
       decoder_1_out4, decoder_1_out5, decoder_1_out6, decoder_1_out7, not_1_out, not_2_out, not_3_out,
       or_1_out, xor_1_out;
  wire [2:0] C_q;

  not not_1 (not_1_out, en);
  Clock clock_1 (.out(clock_1_out));
  not not_2 (not_2_out, C_q[0]);
  and and_1 (and_1_out, en, not_2_out, not_3_out);
  not not_3 (not_3_out, C_q[1]);
  and and_2 (and_2_out, not_1_out, C_q[0], C_q[1]);
  or or_1 (or_1_out, and_1_out, and_2_out);
  xor xor_1 (xor_1_out, en, C_q[0]);
  J_K_Flip_Flop A (.J(or_1_out), .clk(clock_1_out), .K(or_1_out), .Q(C_q[2]));  // open: Qn, preset, en, reset
  J_K_Flip_Flop B (.J(xor_1_out), .clk(clock_1_out), .K(xor_1_out), .Q(C_q[1]));  // open: Qn, preset, en, reset
  J_K_Flip_Flop C (.J(1'b1), .clk(clock_1_out), .K(1'b1), .Q(C_q[0]));  // open: Qn, preset, en, reset
  Decoder #(.select(3)) decoder_1 (
    .out0(decoder_1_out0), .out1(decoder_1_out1), .out2(decoder_1_out2), .out3(decoder_1_out3),
    .out4(decoder_1_out4), .out5(decoder_1_out5), .out6(decoder_1_out6), .out7(decoder_1_out7), .sel(C_q));  // open: en
  Hex_Digit_Display hex_digit_display_1 (.value({1'b0, C_q}));  // open: dp
  LED led_1 (.in(decoder_1_out0));
  LED led_2 (.in(decoder_1_out1));
  LED led_3 (.in(decoder_1_out2));
  LED led_4 (.in(decoder_1_out3));
  LED led_5 (.in(decoder_1_out4));
  LED led_6 (.in(decoder_1_out5));
  LED led_7 (.in(decoder_1_out6));
  LED led_8 (.in(decoder_1_out7));
endmodule
