// Logisim project updown counter_LED_subcircuit.circ as structural Verilog: 2 circuits, main circuit main
module main (
  input  _1,
  input  in_2,
  input  _2,
  input  _3,
  input  _4,
  input  in_6,
  input  _5,
  input  _6,
  input  in_9,
  input  _7,
  input  in_11,
  input  Emergency
);

  wire and_1_out, and_2_out, and_3_out, and_4_out, and_5_out, and_6_out, and_7_out, button_1_out,
       clock_1_out, comparator_1_eq, j_k_ff_1_qn, j_k_ff_2_qn, led_circuit_1_out_5, led_circuit_1_out_6,
       led_circuit_1_out_7, led_circuit_1_out_8, led_circuit_1_out_9, led_circuit_1_out_10,
       led_circuit_1_out_11, led_circuit_1_out_12, nand_1_out, not_1_out, not_2_out, not_4_out, or_1_out,
       or_3_out, or_4_out, xnor_1_out, xnor_2_out, xnor_3_out;
  wire [0:0] comparator_2_gt, comparator_2_lt, or_2_out;
  wire [2:0] j_k_ff_1_q, priority_encoder_1_out;

  Button button_1 (.out(button_1_out));
  not not_1 (not_1_out, Emergency);
  Priority_Encoder priority_encoder_1 (
    .in1(_1), .in2(_2), .in3(_3), .in4(_4), .in5(_5), .in6(_6), .in7(_7), .out(priority_encoder_1_out));  // open: in0, en_in, gs, en_out
  or or_1 (or_1_out, priority_encoder_1_out[0], priority_encoder_1_out[1], priority_encoder_1_out[2]);
  Comparator #(.width(3)) comparator_1 (
    .a(priority_encoder_1_out), .b(j_k_ff_1_q), .eq(comparator_1_eq));  // open: gt, lt
  Comparator #(.width(3), .mode("unsigned")) comparator_2 (
    .a(priority_encoder_1_out), .b(j_k_ff_1_q), .gt(comparator_2_gt[0]), .lt(comparator_2_lt[0]));  // open: eq
  or or_2 (or_2_out[0], comparator_1_eq, button_1_out);
  Clock clock_1 (.out(clock_1_out));
  Hex_Digit_Display hex_digit_display_1 (.value({{3{in_2}}, comparator_2_gt[0]}));  // open: dp
  Hex_Digit_Display hex_digit_display_2 (.value({{3{in_6}}, comparator_2_lt[0]}));  // open: dp
  Hex_Digit_Display hex_digit_display_3 (.value({{3{in_11}}, or_2_out[0]}));  // open: dp
  not not_2 (not_2_out, clock_1_out);
  xnor xnor_1 (xnor_1_out, j_k_ff_1_q[0], priority_encoder_1_out[0]);
  xnor xnor_2 (xnor_2_out, j_k_ff_1_q[1], priority_encoder_1_out[1]);
  xnor xnor_3 (xnor_3_out, j_k_ff_1_q[2], priority_encoder_1_out[2]);
  J_K_Flip_Flop j_k_ff_1 (
    .J(or_1_out), .clk(not_2_out), .K(or_1_out), .Q(j_k_ff_1_q[0]), .Qn(j_k_ff_1_qn), .en(and_1_out));  // open: preset, reset
  and and_1 (and_1_out, not_1_out, nand_1_out);
  // NOT_Gate not_3 has open pins: in=or_1_out, out=open
  nand nand_1 (nand_1_out, xnor_1_out, xnor_2_out, xnor_3_out);
  not not_4 (not_4_out, comparator_2_gt[0]);
  J_K_Flip_Flop j_k_ff_2 (
    .J(or_4_out), .clk(not_2_out), .K(or_4_out), .Q(j_k_ff_1_q[1]), .Qn(j_k_ff_2_qn), .en(and_2_out));  // open: preset, reset
  and and_2 (and_2_out, not_1_out, nand_1_out);
  and and_3 (and_3_out, comparator_2_gt[0], j_k_ff_1_q[1], j_k_ff_1_q[0]);
  and and_4 (and_4_out, j_k_ff_2_qn, j_k_ff_1_qn, not_4_out);
  or or_3 (or_3_out, and_3_out, and_4_out);
  and and_5 (and_5_out, comparator_2_gt[0], j_k_ff_1_q[0]);
  and and_6 (and_6_out, j_k_ff_1_qn, not_4_out);
  J_K_Flip_Flop j_k_ff_3 (
    .J(or_3_out), .clk(not_2_out), .K(or_3_out), .Q(j_k_ff_1_q[2]), .en(and_7_out));  // open: Qn, preset, reset
  and and_7 (and_7_out, not_1_out, nand_1_out);
  or or_4 (or_4_out, and_5_out, and_6_out);
  LED_circuit led_circuit_1 (
    .in_1(j_k_ff_1_q[0]), .in_2(j_k_ff_1_q[1]), .in_3(j_k_ff_1_q[2]), .in_4(in_9),
    .out_5(led_circuit_1_out_5), .out_6(led_circuit_1_out_6), .out_7(led_circuit_1_out_7),
    .out_8(led_circuit_1_out_8), .out_9(led_circuit_1_out_9), .out_10(led_circuit_1_out_10),
    .out_11(led_circuit_1_out_11), .out_12(led_circuit_1_out_12));
  Hex_Digit_Display hex_digit_display_4 (.value({in_9, j_k_ff_1_q}));  // open: dp
  LED led_1 (.in(led_circuit_1_out_5));
  LED led_2 (.in(led_circuit_1_out_6));
  LED led_3 (.in(led_circuit_1_out_7));
  LED led_4 (.in(led_circuit_1_out_8));
  LED led_5 (.in(led_circuit_1_out_9));
  LED led_6 (.in(led_circuit_1_out_10));
  LED led_7 (.in(led_circuit_1_out_11));
  LED led_8 (.in(led_circuit_1_out_12));

  // Notes on the sheet:
  //   Boarding Button
  //   Rising
  //   Falling
  //   Door
endmodule

module LED_circuit (
  input  in_1,
  input  in_2,
  input  in_3,
  input  in_4,
  output out_5,
  output out_6,
  output out_7,
  output out_8,
  output out_9,
  output out_10,
  output out_11,
  output out_12
);

  wire not_1_out, not_2_out, not_3_out, not_4_out, not_5_out, not_6_out, not_7_out, not_8_out, not_9_out,
       not_10_out, not_11_out, not_12_out, or_1_out, or_2_out, or_3_out, or_4_out, or_5_out, or_6_out,
       or_7_out, or_8_out;

  not not_1 (not_1_out, in_1);
  not not_2 (not_2_out, in_2);
  not not_3 (not_3_out, in_1);
  not not_4 (not_4_out, in_2);
  not not_5 (not_5_out, in_3);
  not not_6 (not_6_out, in_1);
  not not_7 (not_7_out, in_3);
  not not_8 (not_8_out, in_2);
  not not_9 (not_9_out, in_3);
  not not_10 (not_10_out, in_1);
  not not_11 (not_11_out, in_2);
  not not_12 (not_12_out, in_3);
  or or_1 (or_1_out, in_1, in_2, in_3, in_4);
  or or_2 (or_2_out, not_1_out, in_2, in_3, in_4);
  or or_3 (or_3_out, in_1, not_2_out, in_3, in_4);
  or or_4 (or_4_out, not_3_out, not_4_out, in_3, in_4);
  or or_5 (or_5_out, in_1, in_2, not_5_out, in_4);
  or or_6 (or_6_out, not_6_out, in_2, not_7_out, in_4);
  or or_7 (or_7_out, in_1, not_8_out, not_9_out, in_4);
  or or_8 (or_8_out, not_10_out, not_11_out, not_12_out, in_4);
  not not_13 (out_5, or_1_out);
  not not_14 (out_6, or_2_out);
  not not_15 (out_7, or_3_out);
  not not_16 (out_8, or_4_out);
  not not_17 (out_9, or_5_out);
  not not_18 (out_10, or_6_out);
  not not_19 (out_11, or_7_out);
  not not_20 (out_12, or_8_out);
endmodule
