// Logisim project updown counter_LED_subcircuit_Fina_2.circ as structural Verilog: 3 circuits, main circuit main
module main (
  input  _1,
  input  in_2,
  input  _2,
  input  _3,
  input  _4,
  input  in_6,
  input  _5,
  input  _6,
  input  in_9,
  input  _7,
  input  in_11,
  input  Emergency
);

  wire button_1_out, button_2_out, clock_1_out, comparator_1_eq, comparator_2_eq, led_circuit_1_out_6,
       led_circuit_1_out_7, led_circuit_1_out_8, led_circuit_1_out_9, led_circuit_1_out_10,
       led_circuit_1_out_11, led_circuit_1_out_12, not_1_out, not_2_out, not_3_out, not_4_out, or_1_out;
  wire [0:0] comparator_1_gt, comparator_1_lt, or_2_out;
  wire [2:0] priority_encoder_1_out, up_down_counter_1_out_10;

  Button button_1 (.out(button_1_out));
  Button button_2 (.out(button_2_out));
  not not_1 (not_1_out, Emergency);
  Priority_Encoder priority_encoder_1 (
    .in0(button_1_out), .in1(_1), .in2(_2), .in3(_3), .in4(_4), .in5(_5), .in6(_6), .in7(_7),
    .out(priority_encoder_1_out));  // open: en_in, gs, en_out
  or or_1 (or_1_out, priority_encoder_1_out[0], priority_encoder_1_out[1], priority_encoder_1_out[2]);
  Comparator #(.width(3), .mode("unsigned")) comparator_1 (
    .a(priority_encoder_1_out), .b(up_down_counter_1_out_10), .gt(comparator_1_gt[0]), .eq(comparator_1_eq),
    .lt(comparator_1_lt[0]));
  or or_2 (or_2_out[0], comparator_1_eq, button_2_out);
  Clock clock_1 (.out(clock_1_out));
  Comparator #(.width(3), .mode("unsigned")) comparator_2 (
    .a(up_down_counter_1_out_10), .b(priority_encoder_1_out), .eq(comparator_2_eq));  // open: gt, lt
  Hex_Digit_Display hex_digit_display_1 (.value({{3{in_2}}, comparator_1_gt[0]}));  // open: dp
  Hex_Digit_Display hex_digit_display_2 (.value({{3{in_6}}, comparator_1_lt[0]}));  // open: dp
  Hex_Digit_Display hex_digit_display_3 (.value({{3{in_11}}, or_2_out[0]}));  // open: dp
  not not_2 (not_2_out, clock_1_out);
  Up_Down_Counter up_down_counter_1 (
    .in_1(comparator_1_gt[0]), .in_2(or_1_out), .in_3(not_2_out), .in_8(not_1_out), .in_6(not_3_out),
    .in_4(not_1_out), .in_9(not_3_out), .in_5(not_1_out), .in_7(not_3_out),
    .out_10(up_down_counter_1_out_10[0]), .out_11(up_down_counter_1_out_10[1]),
    .out_12(up_down_counter_1_out_10[2]));
  not not_3 (not_3_out, comparator_2_eq);
  Hex_Digit_Display hex_digit_display_4 (.value({in_9, up_down_counter_1_out_10}));  // open: dp
  LED_circuit led_circuit_1 (
    .in_1(up_down_counter_1_out_10[0]), .in_2(up_down_counter_1_out_10[1]),
    .in_3(up_down_counter_1_out_10[2]), .in_4(in_9), .out_6(led_circuit_1_out_6),
    .out_7(led_circuit_1_out_7), .out_8(led_circuit_1_out_8), .out_9(led_circuit_1_out_9),
    .out_10(led_circuit_1_out_10), .out_11(led_circuit_1_out_11), .out_12(led_circuit_1_out_12));  // open: out_5
  not not_4 (not_4_out, not_1_out);
  LED led_1 (.in(led_circuit_1_out_6));
  LED led_2 (.in(led_circuit_1_out_7));
  LED led_3 (.in(led_circuit_1_out_8));
  LED led_4 (.in(led_circuit_1_out_9));
  LED led_5 (.in(led_circuit_1_out_10));
  LED led_6 (.in(led_circuit_1_out_11));
  LED led_7 (.in(led_circuit_1_out_12));
  LED led_8 (.in(not_4_out));

  // Notes on the sheet:
  //   Reset
  //   Boarding Button
  //   Rising
  //   Falling
  //   Door
  //   Up/Down
  //   Counter
  //   LED_circuit
  //   1
  //   2
  //   3
  //   4
  //   5
  //   6
  //   7
  //   Emergency
endmodule

module LED_circuit (
  input  in_1,
  input  in_2,
  input  in_3,
  input  in_4,
  output out_5,
  output out_6,
  output out_7,
  output out_8,
  output out_9,
  output out_10,
  output out_11,
  output out_12
);

  wire not_1_out, not_2_out, not_3_out, not_4_out, not_5_out, not_6_out, not_7_out, not_8_out, not_9_out,
       not_10_out, not_11_out, not_12_out, or_1_out, or_2_out, or_3_out, or_4_out, or_5_out, or_6_out,
       or_7_out, or_8_out;

  not not_1 (not_1_out, in_1);
  not not_2 (not_2_out, in_2);
  not not_3 (not_3_out, in_1);
  not not_4 (not_4_out, in_2);
  not not_5 (not_5_out, in_3);
  not not_6 (not_6_out, in_1);
  not not_7 (not_7_out, in_3);
  not not_8 (not_8_out, in_2);
  not not_9 (not_9_out, in_3);
  not not_10 (not_10_out, in_1);
  not not_11 (not_11_out, in_2);
  not not_12 (not_12_out, in_3);
  or or_1 (or_1_out, in_1, in_2, in_3, in_4);
  or or_2 (or_2_out, not_1_out, in_2, in_3, in_4);
  or or_3 (or_3_out, in_1, not_2_out, in_3, in_4);
  or or_4 (or_4_out, not_3_out, not_4_out, in_3, in_4);
  or or_5 (or_5_out, in_1, in_2, not_5_out, in_4);
  or or_6 (or_6_out, not_6_out, in_2, not_7_out, in_4);
  or or_7 (or_7_out, in_1, not_8_out, not_9_out, in_4);
  or or_8 (or_8_out, not_10_out, not_11_out, not_12_out, in_4);
  not not_13 (out_5, or_1_out);
  not not_14 (out_6, or_2_out);
  not not_15 (out_7, or_3_out);
  not not_16 (out_8, or_4_out);
  not not_17 (out_9, or_5_out);
  not not_18 (out_10, or_6_out);
  not not_19 (out_11, or_7_out);
  not not_20 (out_12, or_8_out);
endmodule

module Up_Down_Counter (
  input  in_1,
  input  in_2,
  input  in_3,
  input  in_4,
  input  in_5,
  input  in_6,
  input  in_7,
  input  in_8,
  input  in_9,
  output out_10,
  output out_11,
  output out_12
);

  wire and_1_out, and_2_out, and_3_out, and_4_out, and_5_out, and_6_out, and_7_out, j_k_ff_1_qn, j_k_ff_2_qn,
       not_1_out, not_2_out, or_1_out, or_2_out;

  not not_1 (not_1_out, in_2);
  not not_2 (not_2_out, in_1);
  J_K_Flip_Flop j_k_ff_1 (
    .J(in_2), .clk(in_3), .K(in_2), .Q(out_10), .Qn(j_k_ff_1_qn), .preset(not_1_out), .en(and_1_out));  // open: reset
  and and_1 (and_1_out, in_8, in_6);
  J_K_Flip_Flop j_k_ff_2 (
    .J(or_2_out), .clk(in_3), .K(or_2_out), .Q(out_11), .Qn(j_k_ff_2_qn), .en(and_2_out), .reset(not_1_out));  // open: preset
  and and_2 (and_2_out, in_4, in_9);
  and and_3 (and_3_out, in_1, out_11, out_10);
  and and_4 (and_4_out, j_k_ff_2_qn, j_k_ff_1_qn, not_2_out);
  or or_1 (or_1_out, and_3_out, and_4_out);
  and and_5 (and_5_out, in_5, in_7);
  and and_6 (and_6_out, in_1, out_10);
  and and_7 (and_7_out, j_k_ff_1_qn, not_2_out);
  J_K_Flip_Flop j_k_ff_3 (
    .J(or_1_out), .clk(in_3), .K(or_1_out), .Q(out_12), .en(and_5_out), .reset(not_1_out));  // open: Qn, preset
  or or_2 (or_2_out, and_6_out, and_7_out);
endmodule
